// Logisim project RV.circ as structural Verilog: 5 circuits, main circuit main
module main (
  input  in_1,
  input  [31:0] in_2,
  input  in_3,
  input  RESET
);

  wire CLK_out;
  wire [31:0] fetch_1_instr, fetch_1_pc, fetch_1_pc4;

  Clock CLK (.out(CLK_out));
  fetch fetch_1 (
    .PC_SRC(in_1), .BR_TGT(in_2), .CLK(CLK_out), .RESET(RESET), .STALL_F(in_3), .PC(fetch_1_pc),
    .INSTR(fetch_1_instr), .PC4(fetch_1_pc4));
  decode decode_1 (
    .PC(fetch_1_pc), .INSTR(fetch_1_instr), .PC4(fetch_1_pc4), .CLK(CLK_out), .RESET(RESET));  // open: STALL_D, AD, WD, WE
endmodule

module fetch (
  input  PC_SRC,
  input  [31:0] BR_TGT,
  input  CLK,
  input  RESET,
  input  STALL_F,
  output [31:0] PC,
  output [31:0] INSTR,
  output [31:0] PC4
);

  wire [31:0] multiplexer_1_out;

  Register #(.width(32)) PC_REG (.D(multiplexer_1_out), .en(STALL_F), .clk(CLK), .Q(PC), .clr(RESET));
  Multiplexer #(.width(32)) multiplexer_1 (.in0(PC4), .in1(BR_TGT), .out(multiplexer_1_out), .sel(PC_SRC));
  Adder #(.width(32)) adder_1 (.a(PC), .b(32'h4), .out(PC4));  // open: cin, cout
  ROM #(.addrWidth(16), .dataWidth(32)) IMEM (.addr(PC[17:2]), .data(INSTR));
endmodule

module decode (
  input  [31:0] PC,
  input  [31:0] INSTR,
  input  [31:0] PC4,
  input  CLK,
  input  RESET,
  input  STALL_D,
  input  [4:0] AD,
  input  [31:0] WD,
  input  WE
);

  wire [31:0] register_2_q;

  Register #(.width(32)) register_1 (.D(PC), .en(STALL_D), .clk(CLK), .clr(RESET));  // open: Q
  Register #(.width(32)) register_2 (.D(INSTR), .en(STALL_D), .clk(CLK), .Q(register_2_q), .clr(RESET));
  Register #(.width(32)) register_3 (.D(PC4), .en(STALL_D), .clk(CLK), .clr(RESET));  // open: Q
  control control_1 (.INSTR(register_2_q));  // open: REG_WRITE, RESULT_SRC, MEM_WRITE, JUMP, BRANCH, ALU_CTRL, ALU_SRC, IMM_SRC
  rf rf_1 (
    .CLK(CLK), .RESET(RESET), .WE(WE), .AD(AD), .AS1(register_2_q[19:15]), .AS2(register_2_q[24:20]), .D(WD));  // open: S1, S2
endmodule

module control (
  input  [31:0] INSTR,
  output REG_WRITE,
  output [1:0] RESULT_SRC,
  output MEM_WRITE,
  output JUMP,
  output BRANCH,
  output [2:0] ALU_CTRL,
  output ALU_SRC,
  output [1:0] IMM_SRC
);
endmodule

module rf (
  input  CLK,
  input  RESET,
  input  WE,
  input  [4:0] AD,
  input  [4:0] AS1,
  input  [4:0] AS2,
  input  [31:0] D,
  output [31:0] S1,
  output [31:0] S2
);

  wire [31:0] decoder_1_out0, decoder_2_out0, decoder_3_out0, register_1_q, register_2_q, register_3_q,
       register_4_q, register_5_q, register_6_q, register_7_q, register_8_q, register_9_q, register_10_q,
       register_11_q, register_12_q, register_13_q, register_14_q, register_15_q, register_16_q,
       register_17_q, register_18_q, register_19_q, register_20_q, register_21_q, register_22_q,
       register_23_q, register_24_q, register_25_q, register_26_q, register_27_q, register_28_q,
       register_29_q, register_30_q, register_31_q;

  Decoder #(.select(5)) decoder_1 (
    .out0(decoder_1_out0[0]), .out1(decoder_1_out0[1]), .out2(decoder_1_out0[2]), .out3(decoder_1_out0[3]),
    .out4(decoder_1_out0[4]), .out5(decoder_1_out0[5]), .out6(decoder_1_out0[6]), .out7(decoder_1_out0[7]),
    .out8(decoder_1_out0[8]), .out9(decoder_1_out0[9]), .out10(decoder_1_out0[10]),
    .out11(decoder_1_out0[11]), .out12(decoder_1_out0[12]), .out13(decoder_1_out0[13]),
    .out14(decoder_1_out0[14]), .out15(decoder_1_out0[15]), .out16(decoder_1_out0[16]),
    .out17(decoder_1_out0[17]), .out18(decoder_1_out0[18]), .out19(decoder_1_out0[19]),
    .out20(decoder_1_out0[20]), .out21(decoder_1_out0[21]), .out22(decoder_1_out0[22]),
    .out23(decoder_1_out0[23]), .out24(decoder_1_out0[24]), .out25(decoder_1_out0[25]),
    .out26(decoder_1_out0[26]), .out27(decoder_1_out0[27]), .out28(decoder_1_out0[28]),
    .out29(decoder_1_out0[29]), .out30(decoder_1_out0[30]), .out31(decoder_1_out0[31]), .sel(AD), .en(WE));
  Decoder #(.enable("false"), .select(5)) decoder_2 (
    .out0(decoder_2_out0[0]), .out1(decoder_2_out0[1]), .out2(decoder_2_out0[2]), .out3(decoder_2_out0[3]),
    .out4(decoder_2_out0[4]), .out5(decoder_2_out0[5]), .out6(decoder_2_out0[6]), .out7(decoder_2_out0[7]),
    .out8(decoder_2_out0[8]), .out9(decoder_2_out0[9]), .out10(decoder_2_out0[10]),
    .out11(decoder_2_out0[11]), .out12(decoder_2_out0[12]), .out13(decoder_2_out0[13]),
    .out14(decoder_2_out0[14]), .out15(decoder_2_out0[15]), .out16(decoder_2_out0[16]),
    .out17(decoder_2_out0[17]), .out18(decoder_2_out0[18]), .out19(decoder_2_out0[19]),
    .out20(decoder_2_out0[20]), .out21(decoder_2_out0[21]), .out22(decoder_2_out0[22]),
    .out23(decoder_2_out0[23]), .out24(decoder_2_out0[24]), .out25(decoder_2_out0[25]),
    .out26(decoder_2_out0[26]), .out27(decoder_2_out0[27]), .out28(decoder_2_out0[28]),
    .out29(decoder_2_out0[29]), .out30(decoder_2_out0[30]), .out31(decoder_2_out0[31]), .sel(AS1));
  Decoder #(.enable("false"), .select(5)) decoder_3 (
    .out0(decoder_3_out0[0]), .out1(decoder_3_out0[1]), .out2(decoder_3_out0[2]), .out3(decoder_3_out0[3]),
    .out4(decoder_3_out0[4]), .out5(decoder_3_out0[5]), .out6(decoder_3_out0[6]), .out7(decoder_3_out0[7]),
    .out8(decoder_3_out0[8]), .out9(decoder_3_out0[9]), .out10(decoder_3_out0[10]),
    .out11(decoder_3_out0[11]), .out12(decoder_3_out0[12]), .out13(decoder_3_out0[13]),
    .out14(decoder_3_out0[14]), .out15(decoder_3_out0[15]), .out16(decoder_3_out0[16]),
    .out17(decoder_3_out0[17]), .out18(decoder_3_out0[18]), .out19(decoder_3_out0[19]),
    .out20(decoder_3_out0[20]), .out21(decoder_3_out0[21]), .out22(decoder_3_out0[22]),
    .out23(decoder_3_out0[23]), .out24(decoder_3_out0[24]), .out25(decoder_3_out0[25]),
    .out26(decoder_3_out0[26]), .out27(decoder_3_out0[27]), .out28(decoder_3_out0[28]),
    .out29(decoder_3_out0[29]), .out30(decoder_3_out0[30]), .out31(decoder_3_out0[31]), .sel(AS2));
  Register #(.width(32)) register_1 (.D(D), .en(decoder_1_out0[1]), .clk(CLK), .Q(register_1_q), .clr(RESET));
  Register #(.width(32)) register_2 (.D(D), .en(decoder_1_out0[2]), .clk(CLK), .Q(register_2_q), .clr(RESET));
  Register #(.width(32)) register_3 (.D(D), .en(decoder_1_out0[3]), .clk(CLK), .Q(register_3_q), .clr(RESET));
  Register #(.width(32)) register_4 (.D(D), .en(decoder_1_out0[4]), .clk(CLK), .Q(register_4_q), .clr(RESET));
  Register #(.width(32)) register_5 (.D(D), .en(decoder_1_out0[5]), .clk(CLK), .Q(register_5_q), .clr(RESET));
  Register #(.width(32)) register_6 (.D(D), .en(decoder_1_out0[6]), .clk(CLK), .Q(register_6_q), .clr(RESET));
  Register #(.width(32)) register_7 (.D(D), .en(decoder_1_out0[7]), .clk(CLK), .Q(register_7_q), .clr(RESET));
  assign S1 = decoder_2_out0[0] ? {32{1'b0}} : 32'bz;  // Controlled_Buffer controlled_buffer_1
  assign S2 = decoder_3_out0[0] ? {32{1'b0}} : 32'bz;  // Controlled_Buffer controlled_buffer_2
  assign S1 = decoder_2_out0[1] ? register_1_q : 32'bz;  // Controlled_Buffer controlled_buffer_3
  assign S2 = decoder_3_out0[1] ? register_1_q : 32'bz;  // Controlled_Buffer controlled_buffer_4
  assign S1 = decoder_2_out0[2] ? register_2_q : 32'bz;  // Controlled_Buffer controlled_buffer_5
  assign S2 = decoder_3_out0[2] ? register_2_q : 32'bz;  // Controlled_Buffer controlled_buffer_6
  assign S1 = decoder_2_out0[3] ? register_3_q : 32'bz;  // Controlled_Buffer controlled_buffer_7
  assign S2 = decoder_3_out0[3] ? register_3_q : 32'bz;  // Controlled_Buffer controlled_buffer_8
  assign S1 = decoder_2_out0[4] ? register_4_q : 32'bz;  // Controlled_Buffer controlled_buffer_9
  assign S2 = decoder_3_out0[4] ? register_4_q : 32'bz;  // Controlled_Buffer controlled_buffer_10
  assign S1 = decoder_2_out0[5] ? register_5_q : 32'bz;  // Controlled_Buffer controlled_buffer_11
  assign S2 = decoder_3_out0[5] ? register_5_q : 32'bz;  // Controlled_Buffer controlled_buffer_12
  assign S1 = decoder_2_out0[6] ? register_6_q : 32'bz;  // Controlled_Buffer controlled_buffer_13
  assign S2 = decoder_3_out0[6] ? register_6_q : 32'bz;  // Controlled_Buffer controlled_buffer_14
  assign S1 = decoder_2_out0[7] ? register_7_q : 32'bz;  // Controlled_Buffer controlled_buffer_15
  assign S2 = decoder_3_out0[7] ? register_7_q : 32'bz;  // Controlled_Buffer controlled_buffer_16
  Register #(.width(32)) register_8 (.D(D), .en(decoder_1_out0[8]), .clk(CLK), .Q(register_8_q), .clr(RESET));
  Register #(.width(32)) register_9 (.D(D), .en(decoder_1_out0[9]), .clk(CLK), .Q(register_9_q), .clr(RESET));
  Register #(.width(32)) register_10 (.D(D), .en(decoder_1_out0[10]), .clk(CLK), .Q(register_10_q), .clr(RESET));
  Register #(.width(32)) register_11 (.D(D), .en(decoder_1_out0[11]), .clk(CLK), .Q(register_11_q), .clr(RESET));
  Register #(.width(32)) register_12 (.D(D), .en(decoder_1_out0[12]), .clk(CLK), .Q(register_12_q), .clr(RESET));
  Register #(.width(32)) register_13 (.D(D), .en(decoder_1_out0[13]), .clk(CLK), .Q(register_13_q), .clr(RESET));
  Register #(.width(32)) register_14 (.D(D), .en(decoder_1_out0[14]), .clk(CLK), .Q(register_14_q), .clr(RESET));
  Register #(.width(32)) register_15 (.D(D), .en(decoder_1_out0[15]), .clk(CLK), .Q(register_15_q), .clr(RESET));
  assign S1 = decoder_2_out0[8] ? register_8_q : 32'bz;  // Controlled_Buffer controlled_buffer_17
  assign S2 = decoder_3_out0[8] ? register_8_q : 32'bz;  // Controlled_Buffer controlled_buffer_18
  assign S1 = decoder_2_out0[9] ? register_9_q : 32'bz;  // Controlled_Buffer controlled_buffer_19
  assign S2 = decoder_3_out0[9] ? register_9_q : 32'bz;  // Controlled_Buffer controlled_buffer_20
  assign S1 = decoder_2_out0[10] ? register_10_q : 32'bz;  // Controlled_Buffer controlled_buffer_21
  assign S2 = decoder_3_out0[10] ? register_10_q : 32'bz;  // Controlled_Buffer controlled_buffer_22
  assign S1 = decoder_2_out0[11] ? register_11_q : 32'bz;  // Controlled_Buffer controlled_buffer_23
  assign S2 = decoder_3_out0[11] ? register_11_q : 32'bz;  // Controlled_Buffer controlled_buffer_24
  assign S1 = decoder_2_out0[12] ? register_12_q : 32'bz;  // Controlled_Buffer controlled_buffer_25
  assign S2 = decoder_3_out0[12] ? register_12_q : 32'bz;  // Controlled_Buffer controlled_buffer_26
  assign S1 = decoder_2_out0[13] ? register_13_q : 32'bz;  // Controlled_Buffer controlled_buffer_27
  assign S2 = decoder_3_out0[13] ? register_13_q : 32'bz;  // Controlled_Buffer controlled_buffer_28
  assign S1 = decoder_2_out0[14] ? register_14_q : 32'bz;  // Controlled_Buffer controlled_buffer_29
  assign S2 = decoder_3_out0[14] ? register_14_q : 32'bz;  // Controlled_Buffer controlled_buffer_30
  assign S1 = decoder_2_out0[15] ? register_15_q : 32'bz;  // Controlled_Buffer controlled_buffer_31
  assign S2 = decoder_3_out0[15] ? register_15_q : 32'bz;  // Controlled_Buffer controlled_buffer_32
  Register #(.width(32)) register_16 (.D(D), .en(decoder_1_out0[16]), .clk(CLK), .Q(register_16_q), .clr(RESET));
  Register #(.width(32)) register_17 (.D(D), .en(decoder_1_out0[17]), .clk(CLK), .Q(register_17_q), .clr(RESET));
  Register #(.width(32)) register_18 (.D(D), .en(decoder_1_out0[18]), .clk(CLK), .Q(register_18_q), .clr(RESET));
  Register #(.width(32)) register_19 (.D(D), .en(decoder_1_out0[19]), .clk(CLK), .Q(register_19_q), .clr(RESET));
  Register #(.width(32)) register_20 (.D(D), .en(decoder_1_out0[20]), .clk(CLK), .Q(register_20_q), .clr(RESET));
  Register #(.width(32)) register_21 (.D(D), .en(decoder_1_out0[21]), .clk(CLK), .Q(register_21_q), .clr(RESET));
  Register #(.width(32)) register_22 (.D(D), .en(decoder_1_out0[22]), .clk(CLK), .Q(register_22_q), .clr(RESET));
  Register #(.width(32)) register_23 (.D(D), .en(decoder_1_out0[23]), .clk(CLK), .Q(register_23_q), .clr(RESET));
  assign S1 = decoder_2_out0[16] ? register_16_q : 32'bz;  // Controlled_Buffer controlled_buffer_33
  assign S2 = decoder_3_out0[16] ? register_16_q : 32'bz;  // Controlled_Buffer controlled_buffer_34
  assign S1 = decoder_2_out0[17] ? register_17_q : 32'bz;  // Controlled_Buffer controlled_buffer_35
  assign S2 = decoder_3_out0[17] ? register_17_q : 32'bz;  // Controlled_Buffer controlled_buffer_36
  assign S1 = decoder_2_out0[18] ? register_18_q : 32'bz;  // Controlled_Buffer controlled_buffer_37
  assign S2 = decoder_3_out0[18] ? register_18_q : 32'bz;  // Controlled_Buffer controlled_buffer_38
  assign S1 = decoder_2_out0[19] ? register_19_q : 32'bz;  // Controlled_Buffer controlled_buffer_39
  assign S2 = decoder_3_out0[19] ? register_19_q : 32'bz;  // Controlled_Buffer controlled_buffer_40
  assign S1 = decoder_2_out0[20] ? register_20_q : 32'bz;  // Controlled_Buffer controlled_buffer_41
  assign S2 = decoder_3_out0[20] ? register_20_q : 32'bz;  // Controlled_Buffer controlled_buffer_42
  assign S1 = decoder_2_out0[21] ? register_21_q : 32'bz;  // Controlled_Buffer controlled_buffer_43
  assign S2 = decoder_3_out0[21] ? register_21_q : 32'bz;  // Controlled_Buffer controlled_buffer_44
  assign S1 = decoder_2_out0[22] ? register_22_q : 32'bz;  // Controlled_Buffer controlled_buffer_45
  assign S2 = decoder_3_out0[22] ? register_22_q : 32'bz;  // Controlled_Buffer controlled_buffer_46
  assign S1 = decoder_2_out0[23] ? register_23_q : 32'bz;  // Controlled_Buffer controlled_buffer_47
  assign S2 = decoder_3_out0[23] ? register_23_q : 32'bz;  // Controlled_Buffer controlled_buffer_48
  Register #(.width(32)) register_24 (.D(D), .en(decoder_1_out0[24]), .clk(CLK), .Q(register_24_q), .clr(RESET));
  Register #(.width(32)) register_25 (.D(D), .en(decoder_1_out0[25]), .clk(CLK), .Q(register_25_q), .clr(RESET));
  Register #(.width(32)) register_26 (.D(D), .en(decoder_1_out0[26]), .clk(CLK), .Q(register_26_q), .clr(RESET));
  Register #(.width(32)) register_27 (.D(D), .en(decoder_1_out0[27]), .clk(CLK), .Q(register_27_q), .clr(RESET));
  Register #(.width(32)) register_28 (.D(D), .en(decoder_1_out0[28]), .clk(CLK), .Q(register_28_q), .clr(RESET));
  Register #(.width(32)) register_29 (.D(D), .en(decoder_1_out0[29]), .clk(CLK), .Q(register_29_q), .clr(RESET));
  Register #(.width(32)) register_30 (.D(D), .en(decoder_1_out0[30]), .clk(CLK), .Q(register_30_q), .clr(RESET));
  Register #(.width(32)) register_31 (.D(D), .en(decoder_1_out0[31]), .clk(CLK), .Q(register_31_q), .clr(RESET));
  assign S1 = decoder_2_out0[24] ? register_24_q : 32'bz;  // Controlled_Buffer controlled_buffer_49
  assign S2 = decoder_3_out0[24] ? register_24_q : 32'bz;  // Controlled_Buffer controlled_buffer_50
  assign S1 = decoder_2_out0[25] ? register_25_q : 32'bz;  // Controlled_Buffer controlled_buffer_51
  assign S2 = decoder_3_out0[25] ? register_25_q : 32'bz;  // Controlled_Buffer controlled_buffer_52
  assign S1 = decoder_2_out0[26] ? register_26_q : 32'bz;  // Controlled_Buffer controlled_buffer_53
  assign S2 = decoder_3_out0[26] ? register_26_q : 32'bz;  // Controlled_Buffer controlled_buffer_54
  assign S1 = decoder_2_out0[27] ? register_27_q : 32'bz;  // Controlled_Buffer controlled_buffer_55
  assign S2 = decoder_3_out0[27] ? register_27_q : 32'bz;  // Controlled_Buffer controlled_buffer_56
  assign S1 = decoder_2_out0[28] ? register_28_q : 32'bz;  // Controlled_Buffer controlled_buffer_57
  assign S2 = decoder_3_out0[28] ? register_28_q : 32'bz;  // Controlled_Buffer controlled_buffer_58
  assign S1 = decoder_2_out0[29] ? register_29_q : 32'bz;  // Controlled_Buffer controlled_buffer_59
  assign S2 = decoder_3_out0[29] ? register_29_q : 32'bz;  // Controlled_Buffer controlled_buffer_60
  assign S1 = decoder_2_out0[30] ? register_30_q : 32'bz;  // Controlled_Buffer controlled_buffer_61
  assign S2 = decoder_3_out0[30] ? register_30_q : 32'bz;  // Controlled_Buffer controlled_buffer_62
  assign S1 = decoder_2_out0[31] ? register_31_q : 32'bz;  // Controlled_Buffer controlled_buffer_63
  assign S2 = decoder_3_out0[31] ? register_31_q : 32'bz;  // Controlled_Buffer controlled_buffer_64
endmodule
